# Fritzing sketch flame_frame_2 (saved by Fritzing 0.9.3b)
circuit board: 5.5cm x 5.5cm
breadboards: 1

parts:
  Teensy_3_3 = Teensy 3.1
  J7 = female pin header, 6 pins [form="♀ (female)"]
  RX = female pin header, 6 pins [form="♀ (female)"]
  J9 = female pin header, 2 pins [form="♀ (female)"]
  J11 = female pin header, 2 pins [form="♀ (female)"]
  LED5 = LED - 3mm [color="Red (633nm)" package="3 mm [THT]"]
  LED6 = LED - 3mm [color="Red (633nm)" package="3 mm [THT]"]
  LED7 = LED - 3mm [color="Red (633nm)" package="3 mm [THT]"]
  LED8 = LED - 3mm [color="Red (633nm)" package="3 mm [THT]"]
  R1 = Resistor [tolerance=±5% resistance=220 package="1206 [SMD]"]
  R2 = Resistor [tolerance=±5% resistance=220 package="1206 [SMD]"]
  R3 = Resistor [tolerance=±5% resistance=220 package="1206 [SMD]"]
  R4 = Resistor [tolerance=±5% resistance=220 package="1206 [SMD]"]
  GY2 = MPU-6050 Board GY-521 [form="♀ (female)" package=THT]
  RX4 = female pin header, 4 pins [form="♀ (female)"]
  J8 = female pin header, 4 pins [form="♀ (female)"]
  RX3 = female pin header, 4 pins [form="♀ (female)"]

nets:
  N1: Teensy_3_3.GND, J9.pin2, J11.pin1, R4.Pin_0, GY2.pin2
  N2: Teensy_3_3.D0, J7.pin1
  N3: Teensy_3_3.D1, J7.pin2
  N4: Teensy_3_3.D2, J7.pin3
  N5: Teensy_3_3.D3, J7.pin4
  N6: Teensy_3_3.D4, J7.pin5
  N7: Teensy_3_3.D5, J7.pin6
  N8: Teensy_3_3.D6, RX.pin1
  N9: Teensy_3_3.D7, RX.pin2
  N10: Teensy_3_3.D9, RX.pin3
  N11: Teensy_3_3.D10, RX.pin4
  N12: Teensy_3_3.D11, RX.pin5
  N13: Teensy_3_3.D12, RX.pin6
  N14: Teensy_3_3.A0/D14, GY2.pin1
  N15: Teensy_3_3.A1/D15, GY2.pin8
  N16: Teensy_3_3.A4/D18, GY2.pin4
  N17: Teensy_3_3.A5/D19, GY2.pin3
  N18: Teensy_3_3.A6/D20, LED8.cathode, J8.pin4
  N19: Teensy_3_3.A7/D21, LED7.cathode, J8.pin3
  N20: Teensy_3_3.A8/D22, LED6.cathode, J8.pin2
  N21: Teensy_3_3.A9/D23, LED5.cathode, J8.pin1
  N22: Teensy_3_3.Vin, J9.pin1, J11.pin2, RX4.pin1
  N23: LED5.anode, R3.Pin_0, R4.Pin_1
  N24: LED6.anode, R2.Pin_0
  N25: LED7.anode, R1.Pin_1
  N26: LED8.anode, R3.Pin_1
  N27: R1.Pin_0, R2.Pin_1, RX3.pin1, RX3.pin2, RX3.pin3, RX3.pin4
  N28: RX4.pin2, RX4.pin3, RX4.pin4

notes:
  -+
  f450 v1
  - + s
  pwr | servobus
  5V
  0 1 2 3 4 5

custom parts:
  MPU-6050 Board GY-521: Acelerometro y Giroscopio MPU-6050 Board GY-521
