# Fritzing sketch flame_frame_3 (saved by Fritzing 0.9.3b)
circuit board: 5.5cm x 5.5cm
breadboards: 1

parts:
  J9 = female pin header, 2 pins [form="♀ (female)"]
  J11 = female pin header, 2 pins [form="♀ (female)"]
  Teensy_3_3 = Teensy 3.1
  HC-05 = female pin header, 6 pins [form="♀ (female)"]
  GPS = female pin header, 5 pins [form="♀ (female)"]
  J14 = female pin header, 6 pins [form="♀ (female)"]
  LED1 = smd LED [color="Red (633nm)" package="1206 [SMD]"]
  LED2 = smd LED [color="Red (633nm)" package="1206 [SMD]"]
  LED3 = smd LED [color="Red (633nm)" package="1206 [SMD]"]
  LED4 = smd LED [color="Red (633nm)" package="1206 [SMD]"]
  LED5 = smd LED [color="Red (633nm)" package="1206 [SMD]"]
  LED6 = smd LED [color="Red (633nm)" package="1206 [SMD]"]
  R1 = Resistor [tolerance=±5% resistance=220 package="0805 [SMD]"]
  R2 = Resistor [tolerance=±5% resistance=220 package="0805 [SMD]"]
  R3 = Resistor [tolerance=±5% resistance=220 package="0805 [SMD]"]
  R4 = Resistor [tolerance=±5% resistance=220 package="0805 [SMD]"]
  R5 = Resistor [tolerance=±5% resistance=220 package="0805 [SMD]"]
  R6 = Resistor [tolerance=±5% resistance=220 package="0805 [SMD]"]
  J15 = female pin header, 7 pins [form="♀ (female)"]

nets:
  N1: J9.pin1, J11.pin1, Teensy_3_3.Vin, HC-05.pin5, GPS.pin5
  N2: J9.pin2, J11.pin2, Teensy_3_3.GND, HC-05.pin4, GPS.pin4, R1.Pin_1, R2.Pin_1, R3.Pin_1, R4.Pin_1, R5.Pin_1, R6.Pin_1
  N3: Teensy_3_3.D0, HC-05.pin3
  N4: Teensy_3_3.D1, HC-05.pin2
  N5: Teensy_3_3.D2, J14.pin6, LED1.cathode
  N6: Teensy_3_3.D3, J14.pin5, LED2.cathode
  N7: Teensy_3_3.D4, J14.pin4, LED3.cathode
  N8: Teensy_3_3.D5, J14.pin3, LED4.cathode
  N9: Teensy_3_3.D6, J14.pin2, LED5.cathode
  N10: Teensy_3_3.D7, J14.pin1, LED6.cathode
  N11: Teensy_3_3.D9, GPS.pin3
  N12: Teensy_3_3.D10, GPS.pin2
  N13: Teensy_3_3.A1/D15, J15.pin1
  N14: Teensy_3_3.A4/D18, J15.pin2
  N15: Teensy_3_3.A5/D19, J15.pin3
  N16: Teensy_3_3.A6/D20, J15.pin4
  N17: Teensy_3_3.A7/D21, J15.pin5
  N18: Teensy_3_3.A8/D22, J15.pin6
  N19: Teensy_3_3.A9/D23, J15.pin7
  N20: LED1.anode, R1.Pin_0
  N21: LED2.anode, R2.Pin_0
  N22: LED3.anode, R3.Pin_0
  N23: LED4.anode, R4.Pin_0
  N24: LED5.anode, R5.Pin_0
  N25: LED6.anode, R6.Pin_0

notes:
  -+
  f450 v2
  f450 v1
  rx tx - +
  + - tx rx
