# Fritzing sketch Receiver (saved by Fritzing 0.9.3b)
circuit board: 7.21565cm x 5.50228cm
breadboards: 1

parts:
  Servo_Driver = 16-Channel 12-bit PWM Servo Driver - I2C [part_number=815]
  Vin = Header 4 [package=molex-1x4_lock]
  -_+ = Arduino Uno (Rev3) - ICSP

nets:
  N1: Servo_Driver.SDA, -_+.A4/SDA
  N2: Servo_Driver.SCL, -_+.A5/SCL
  VCC: Servo_Driver.VCC, Vin.4, -_+.5V
  GND: Servo_Driver.GND, Vin.1, Vin.3, -_+.GND

custom parts:
  16-Channel 12-bit PWM Servo Driver - I2C: You want to make a cool robot, maybe a hexapod walker, or maybe just a piece of art with a lot of moving parts. Or maybe you want to drive a lot of LEDs with precise PWM output. Using only two pins, control 16 free-running PWM outputs! You can even chain up 62 breakouts to control up to 992 PWM outputs.
