# Fritzing sketch Transmitter (saved by Fritzing 0.9.3b)
circuit board: 7.33673cm x 5.60655cm
breadboards: 1

parts:
  Transmitter = Arduino Uno (Rev3)
  Teensy_3_2 = Teensy 3.1
  MPU6050 = MPU-6050 Board GY-521 [form="♀ (female)" package=THT]
  S1 = Round Pushbutton

nets:
  N1: Transmitter.A4/SDA, Teensy_3_2.A4/D18, MPU6050.pin4
  N2: Transmitter.A5/SCL, Teensy_3_2.A5/D19, MPU6050.pin3
  GND: Transmitter.GND, Teensy_3_2.GND, MPU6050.pin2, S1.leg1
  N3: Teensy_3_2.D2, MPU6050.pin5
  N4: Teensy_3_2.D6, S1.leg0
  N5: Teensy_3_2.3V3, MPU6050.pin1

custom parts:
  MPU-6050 Board GY-521: Acelerometro y Giroscopio MPU-6050 Board GY-521
