# Fritzing sketch raPID_FC (saved by Fritzing 0.9.3b)
circuit board: 7.29735cm x 5.39684cm
breadboards: 1

parts:
  Teensy_3_2 = Teensy 3.1
  1_2_3_4_5_6_7_8_9_A_B_C = Header 12 [package=1x12_machine-pin-header_lock.004]
  VIN = Header 2 [package=molex-1x2_lock]
  Servo_driver = 16-Channel 12-bit PWM Servo Driver - I2C [part_number=815]
  MPU6050 = MPU-6050 Board GY-521 [form="♀ (female)" package=THT]
  S1 = Round Pushbutton
  R1 = Rotary Potentiometer (Large) [maximum_resistance=100kΩ package=THT]
  1_2_3_4 = Resistor [tolerance=±5% resistance=220 package=THT]
  LED = LED - 3mm [color="Red (633nm)" package="3 mm [THT]"]
  DBG = LED - 3mm [color="Red (633nm)" package="3 mm [THT]"]
  J1 = female pin header, 3 pins [form="♀ (female)"]
  J2 = female pin header, 3 pins [form="♀ (female)"]
  J3 = female pin header, 2 pins [form="♀ (female)"]

nets:
  GND: Teensy_3_2.GND, VIN.1, Servo_driver.GND, MPU6050.pin2, S1.leg1, R1.leg2, LED.anode, J3.pin1
  N1: Teensy_3_2.D0, 1_2_3_4_5_6_7_8_9_A_B_C.1
  N2: Teensy_3_2.D1, 1_2_3_4_5_6_7_8_9_A_B_C.2
  N3: Teensy_3_2.D2, 1_2_3_4_5_6_7_8_9_A_B_C.3
  N4: Teensy_3_2.D3, 1_2_3_4_5_6_7_8_9_A_B_C.4
  N5: Teensy_3_2.D4, 1_2_3_4_5_6_7_8_9_A_B_C.5
  N6: Teensy_3_2.D5, 1_2_3_4_5_6_7_8_9_A_B_C.6
  N7: Teensy_3_2.D6, 1_2_3_4_5_6_7_8_9_A_B_C.7
  N8: Teensy_3_2.D7, 1_2_3_4_5_6_7_8_9_A_B_C.8
  N9: Teensy_3_2.D8, 1_2_3_4_5_6_7_8_9_A_B_C.9
  N10: Teensy_3_2.D9, 1_2_3_4_5_6_7_8_9_A_B_C.10
  N11: Teensy_3_2.D10, 1_2_3_4_5_6_7_8_9_A_B_C.11
  N12: Teensy_3_2.D11, 1_2_3_4_5_6_7_8_9_A_B_C.12
  N13: Teensy_3_2.D12, MPU6050.pin8
  N14: Teensy_3_2.A14/DAC, MPU6050.pin5, J3.pin2
  N15: Teensy_3_2.D13, S1.leg0
  N16: Teensy_3_2.A0/D14, J1.pin1
  N17: Teensy_3_2.A1/D15, R1.wiper
  N18: Teensy_3_2.A2/D16, J1.pin2
  N19: Teensy_3_2.A3/D17, J1.pin3
  N20: Teensy_3_2.A4/D18, Servo_driver.SDA, MPU6050.pin4
  N21: Teensy_3_2.A5/D19, Servo_driver.SCL, MPU6050.pin3
  N22: Teensy_3_2.A6/D20, J2.pin1
  N23: Teensy_3_2.A7/D21, J2.pin2
  N24: Teensy_3_2.A8/D22, DBG.cathode, J2.pin3
  N25: Teensy_3_2.A9/D23, 1_2_3_4.Pin_1, DBG.anode
  N26: Teensy_3_2.3V3, MPU6050.pin1, R1.leg1
  VIN: Teensy_3_2.Vin, VIN.2, Servo_driver.VCC
  N27: Servo_driver.5.0V, Servo_driver.PWRIN
  N28: 1_2_3_4.Pin_0, LED.cathode

notes:
  0 1 2 3
  4 5 6 7
  8 9 A B
  C D E F

custom parts:
  16-Channel 12-bit PWM Servo Driver - I2C: You want to make a cool robot, maybe a hexapod walker, or maybe just a piece of art with a lot of moving parts. Or maybe you want to drive a lot of LEDs with precise PWM output. Using only two pins, control 16 free-running PWM outputs! You can even chain up 62 breakouts to control up to 992 PWM outputs.
  MPU-6050 Board GY-521: Acelerometro y Giroscopio MPU-6050 Board GY-521
