# Fritzing sketch raPID_FC_mini (saved by Fritzing 0.9.3b)
circuit board: 5.60366cm x 2.79097cm
breadboards: 1

parts:
  S_+_- = Basic Servo
  Teensy_3_2 = Teensy 3.1
  MPU-6050 = MPU-6050 Board GY-521 [form="♀ (female)" package=THT]
  J2 = Basic Servo
  J3 = Basic Servo
  OUTPUT = Basic Servo
  1_2_3_4_5_6 = Header 6 [package=molex-1x6-ra]
  LED = LED - 3mm [color="Red (633nm)" package="3 mm [THT]"]
  DBG1 = LED - 3mm [color="Red (633nm)" package="3 mm [THT]"]
  DBG2 = female pin header, 2 pins [form="♀ (female)"]
  RX_GND = female pin header, 1 pin [form="♀ (female)"]
  Pad1 = Pad [width=2 height=2 connect=center]  # not connected
  R1 = Resistor [tolerance=±5% resistance=220 package="1206 [SMD]"]
  R2 = Resistor [tolerance=±5% resistance=220 package="1206 [SMD]"]
  Pad2 = Pad [width=2 height=2 connect=center]

nets:
  GND: S_+_-.gnd, Teensy_3_2.GND, MPU-6050.pin2, J2.gnd, J3.gnd, OUTPUT.gnd, LED.cathode, RX_GND.pin1, R2.Pin_1
  VCC: S_+_-.vcc, Teensy_3_2.Vin, J2.vcc, J3.vcc, OUTPUT.vcc
  N1: S_+_-.pulse, Teensy_3_2.D3
  N2: Teensy_3_2.D0, DBG2.pin2
  N3: Teensy_3_2.D1, DBG2.pin1
  N4: Teensy_3_2.D4, OUTPUT.pulse
  N5: Teensy_3_2.D5, J2.pulse
  N6: Teensy_3_2.D6, J3.pulse
  N7: Teensy_3_2.D7, 1_2_3_4_5_6.6
  N8: Teensy_3_2.D8, 1_2_3_4_5_6.5
  N9: Teensy_3_2.D9, 1_2_3_4_5_6.4
  N10: Teensy_3_2.D10, 1_2_3_4_5_6.3
  N11: Teensy_3_2.D11, 1_2_3_4_5_6.2
  N12: Teensy_3_2.D12, 1_2_3_4_5_6.1
  N13: Teensy_3_2.D13, MPU-6050.pin8
  N14: Teensy_3_2.A4/D18, MPU-6050.pin4
  N15: Teensy_3_2.A5/D19, MPU-6050.pin3
  N16: Teensy_3_2.A6/D20, LED.anode
  N17: Teensy_3_2.A7/D21, R1.Pin_1, R2.Pin_0
  N18: Teensy_3_2.A8/D22, DBG1.anode
  N19: Teensy_3_2.A9/D23, DBG1.cathode
  N20: Teensy_3_2.3V3, MPU-6050.pin1
  N21: R1.Pin_0, Pad2.pad

notes:
  v_bat
  raPID FC mini

custom parts:
  MPU-6050 Board GY-521: Acelerometro y Giroscopio MPU-6050 Board GY-521
