# Fritzing sketch rapid_fc_3.5 (saved by Fritzing 0.9.3b)
circuit board: 8.35282cm x 4.40199cm
breadboards: 1

parts:
  J1 = female pin header, 24 pins [form="♀ (female)"]
  J2 = female pin header, 24 pins [form="♀ (female)"]
  J3 = female pin header, 5 pins [form="♀ (female)"]
  J4 = female pin header, 8 pins [form="♀ (female)"]
  J5 = female pin header, 8 pins [form="♀ (female)"]
  J6 = female pin header, 8 pins [form="♀ (female)"]
  J7 = female pin header, 8 pins [form="♀ (female)"]
  +_- = female pin header, 2 pins [form="♀ (female)"]
  -_+ = female pin header, 2 pins [form="♀ (female)"]
  mpu = female pin header, 8 pins [form="♀ (female)"]
  J8 = female pin header, 8 pins [form="♀ (female)"]
  J9 = female pin header, 8 pins [form="♀ (female)"]
  J10 = female pin header, 8 pins [form="♀ (female)"]
  R1 = Resistor [tolerance=±5% resistance=220 package="0805 [SMD]"]
  R3 = Resistor [tolerance=±5% resistance=220 package="0805 [SMD]"]
  J11 = female pin header, 3 pins [form="♀ (female)"]
  J12 = female pin header, 3 pins [form="♀ (female)"]
  J13 = female pin header, 2 pins [form="♀ (female)"]
  LED = LED - 3mm [color="Red (633nm)" package="3 mm [THT]"]
  J14 = female pin header, 1 pin [form="♀ (female)"]
  3_3_gnd_scl_sda = female pin header, 4 pins [form="♀ (female)"]
  J15 = female pin header, 6 pins [form="♀ (female)"]
  J16 = female pin header, 4 pins [form="♀ (female)"]

nets:
  N1: J1.pin1, mpu.pin3, 3_3_gnd_scl_sda.pin2
  N2: J1.pin2, mpu.pin4, 3_3_gnd_scl_sda.pin1
  N3: J1.pin3, J4.pin1
  N4: J1.pin4, J4.pin2
  N5: J1.pin5, J4.pin3
  N6: J1.pin6, J4.pin4
  N7: J1.pin7, J16.pin1
  N8: J1.pin8, J16.pin2
  N9: J1.pin9, J16.pin3
  N10: J1.pin10, J16.pin4
  N11: J1.pin12, J15.pin1
  N12: J1.pin13, J15.pin2
  N13: J1.pin14, J15.pin3
  N14: J1.pin15, J15.pin4
  N15: J1.pin16, J15.pin5
  N16: J1.pin17, J15.pin6
  N17: J1.pin18, J4.pin5
  N18: J1.pin19, J4.pin6
  N19: J1.pin20, J4.pin7
  N20: J1.pin21, J4.pin8
  N21: J1.pin24, +_-.pin1, -_+.pin1, R1.Pin_0, R3.Pin_0
  N22: J2.pin1, mpu.pin8
  N23: J2.pin2, J10.pin1
  N24: J2.pin3, J10.pin2
  N25: J2.pin4, J10.pin3
  N26: J2.pin5, J10.pin4
  N27: J2.pin6, J10.pin5
  N28: J2.pin7, J10.pin6
  N29: J2.pin8, J10.pin7
  N30: J2.pin9, J10.pin8
  N31: J2.pin10, J12.pin1
  N32: J2.pin11, J13.pin1
  N33: J2.pin12, J13.pin2
  N34: J2.pin13, J11.pin1
  N35: J2.pin14, J7.pin1
  N36: J2.pin15, J7.pin2
  N37: J2.pin16, J7.pin3
  N38: J2.pin17, J7.pin4
  N39: J2.pin18, J7.pin5
  N40: J2.pin19, J7.pin6
  N41: J2.pin20, J7.pin7
  N42: J2.pin21, J7.pin8
  N43: J2.pin22, J14.pin1
  N44: J2.pin23, LED.cathode
  N45: J2.pin24, J6.pin1, J6.pin2, J6.pin3, J6.pin4, J6.pin5, J6.pin6, J6.pin7, J6.pin8, +_-.pin2, -_+.pin2, J8.pin1, J8.pin2, J8.pin3, J8.pin4, J8.pin5, J8.pin6, J8.pin7, J8.pin8, J11.pin3, J12.pin3, LED.anode
  N46: J3.pin2, mpu.pin1, 3_3_gnd_scl_sda.pin4
  N47: J3.pin3, mpu.pin2, 3_3_gnd_scl_sda.pin3
  N48: J5.pin1, J5.pin2, J5.pin3, J5.pin4, J5.pin5, J5.pin6, J5.pin7
  N49: J5.pin8, R3.Pin_1
  N50: J9.pin1, J9.pin2, J9.pin3, J9.pin4, J9.pin5, J9.pin6, J9.pin7, J11.pin2, J12.pin2
  N51: J9.pin8, R1.Pin_1
